# Fritzing sketch Fridge_Alarm_Sketch (saved by Fritzing 0.9.3b)

parts:
  Part1 = Adafruit Trinket M0 [part_number="Adafruit #3500"]
  S4 = Magnetic Door Switch [package=reed_switch_plastic]
  S5 = Magnetic Door Switch [package=reed_switch_plastic]
  J1 = Piezo Speaker  # not connected

nets:
  N1: Part1.D3_A3_PA07_RXD_SCK, S5.2
  N2: Part1.D2_A1_PA09_SCL_MISO, S4.2

notes:
  GND
